# Fritzing sketch Estação Metereológica (saved by Fritzing 0.9.5d)
breadboards: 1

parts:
  M1 = DOIT Esp32 DevKit v1 (30 pins long, 11 pins width) [part_number=ESP32S-PIN30]
  YwRobot_Power_Supply1 = YwRobot Breadboard Power Supply [part_number=545043]
  DHT1 = DHT22 Humidity and Temperature Sensor
  A1 = GY-BMP280 Breakout
  M2 = MQ-135 Air Quality Sensor Module
  LDR1 = LDR LM393 - modulo 4 pinos [package=THT]
  R2 = Resistor [tolerance=±5% resistance=20k package="0805 [SMD]"]
  R3 = Resistor [tolerance=±5% resistance=20k package="0805 [SMD]"]
  R4 = Resistor [tolerance=±5% resistance=20k package="0805 [SMD]"]
  R1 = Resistor [tolerance=±5% resistance=10k package="0805 [SMD]"]

nets:
  GND: M1.GND, YwRobot_Power_Supply1.GND, DHT1.GND, A1.GND, M2.GND, LDR1.GND, R2.Pin_0
  N1: M1.D4, DHT1.DATA, R3.Pin_1, R4.Pin_1
  N2: M1.D21, A1.SDA
  N3: M1.D22, A1.SCL
  N4: M1.D34, LDR1.AO
  N5: M1.D35, R2.Pin_1, R1.Pin_1
  VIN: M1.VIN, YwRobot_Power_Supply1.VCC#5, YwRobot_Power_Supply1.VCC#6, M2.VCC
  VCC: YwRobot_Power_Supply1.VCC#9, YwRobot_Power_Supply1.VCC#10, DHT1.VDD, A1.VCC, LDR1.VCC, R3.Pin_0, R4.Pin_0
  N6: M2.AO, R1.Pin_0

notes:
  5V
  3V3

custom parts:
  DOIT Esp32 DevKit v1 (30 pins long, 11 pins width): The DOIT Esp32 DevKit v1 is one of the development board created by DOIT to evaluate the ESP-WROOM-32 module. It is based on the ESP32 microcontroller that boasts Wifi, Bluetooth, Ethernet and Low Power support all in a single chip. (vanepp) made breadboard work, adjusted pin numbering and labels and reduced size of schematic and cleaned up pcb. This chip is 30pins long (2 x15) and 11 pins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
  YwRobot Breadboard Power Supply: The YwRobot Breadboard Power Supply (MB-V2) has two power rails; they can be 5V or 3V3. Power to the module can be provided through the female USB socket or through the A10 (female) 2.1mm power jack.
  MQ-135 Air Quality Sensor Module: The MQ-135 air quality sensor is one of range of MQ gas sensors that can be used to detect, measure, and monitor a wide range of gases, including NH3, NOx, CO2, benzene, and smoke, present in the atmosphere.
  LDR LM393 - modulo 4 pinos: Representacao vetorial do modulo LDR com LM393, trimpot e quatro terminais AO, DO, GND e VCC. Uso documental; sem modelo SPICE.
